// Logisim project ALU_4bit.circ as structural Verilog: 1 circuit, main circuit alu
module alu (
  input  [3:0] A,
  input  [3:0] B,
  input  [1:0] ALUOp,
  output [3:0] C
);

  wire [3:0] A_B, A_B_t, A_B_t_t, A_B_t_t_t;

  Multiplexer #(.select(2), .width(4)) multiplexer_1 (
    .in0(A_B_t), .in1(A_B_t_t), .in2(A_B), .in3(A_B_t_t_t), .out(C), .sel(ALUOp));  // open: en
  Adder #(.width(4)) adder_1 (.a(A), .b(B), .out(A_B_t));  // open: cin, cout
  Subtractor #(.width(4)) subtractor_1 (.a(A), .b(B), .out(A_B_t_t));  // open: bin, bout
  assign A_B = A & B;  // AND_Gate and_1, 4 bits wide
  assign A_B_t_t_t = A | B;  // OR_Gate or_1, 4 bits wide
endmodule
