// Logisim project CRCgen.circ as structural Verilog: 2 circuits, main circuit 4mod4_1and3
module _4mod4_1and3 (
  input  [3:0] A,
  input  [3:0] B,
  output Q,
  output [2:0] R
);

  wire [3:0] bit_extender_1_out, multiplier_1_out;
  wire [3:3] xor_1_out;

  Multiplier #(.width(4)) multiplier_1 (.a(B), .b(bit_extender_1_out), .out(multiplier_1_out));  // open: cin, cout
  assign bit_extender_1_out = {{3{1'b0}}, A[3]};  // Bit_Extender bit_extender_1
  assign {xor_1_out[3], R} = A ^ multiplier_1_out;  // XOR_Gate xor_1, 4 bits wide

  assign Q = A[3];
endmodule

module CRC (
  input  [7:0] A,
  input  [3:0] B,
  output [10:0] C
);

  wire Q1, Q2, Q3, Q4, Q5, Q6, Q7, Q8;
  wire [2:0] R1, R2, R3, R4, R5, R6, R7;

  _4mod4_1and3 u_4mod4_1and3_1 (.A(A[7:4]), .B(B), .Q(Q1), .R(R1));
  // Probe on Q1
  _4mod4_1and3 u_4mod4_1and3_2 (.A({R1, A[3]}), .B(B), .Q(Q2), .R(R2));
  // Probe on Q2
  _4mod4_1and3 u_4mod4_1and3_3 (.A({R2, A[2]}), .B(B), .Q(Q3), .R(R3));
  // Probe on Q3
  // Probe on Q4
  _4mod4_1and3 u_4mod4_1and3_4 (.A({R3, A[1]}), .B(B), .Q(Q4), .R(R4));
  _4mod4_1and3 u_4mod4_1and3_5 (.A({R4, A[0]}), .B(B), .Q(Q5), .R(R5));
  // Probe on Q5
  _4mod4_1and3 u_4mod4_1and3_6 (.A({R5, 1'b0}), .B(B), .Q(Q6), .R(R6));
  // Probe on Q6
  // Probe on Q7
  _4mod4_1and3 u_4mod4_1and3_7 (.A({R6, 1'b0}), .B(B), .Q(Q7), .R(R7));
  // Probe on Q8
  _4mod4_1and3 u_4mod4_1and3_8 (.A({R7, 1'b0}), .B(B), .Q(Q8), .R(C[2:0]));
  // Probe on R1
  // Probe on R2
  // Probe on R3
  // Probe on R4
  // Probe on R5
  // Probe on R6
  // Probe on R7
  // Probe on C[2:0]
  // Probe on A

  assign C[10:3] = A;

  // Other names for the same wires on the sheet: R8[2:0] = C[2:0]; h = A[0]; g = A[1]; f = A[2]; e = A[3]; d = A[4];
  //   c_t = A[5]; b_t = A[6]; a_t = A[7]
endmodule
