// Logisim project GeneralRegisterFile.circ as structural Verilog: 1 circuit, main circuit grf
module grf (
  input  clk,
  input  reset,
  input  WE,
  input  [4:0] A1,
  input  [4:0] A2,
  input  [4:0] A3,
  input  [31:0] WD,
  output [31:0] RD1,
  output [31:0] RD2
);

  wire en1, en2, en3, en4, en5, en6, en7, en8, en9, en10, en11, en12, en13, en14, en15, en16, en17, en18,
       en19, en20, en21, en22, en23, en24, en25, en26, en27, en28, en29, en30, en31;
  wire [4:0] and_1_out;
  wire [31:0] _1, _2, _3, _4, _5, _6, _7, _8, _9, _10, _11, _12, _13, _14, _15, _16, _17, _18, _19, _20, _21,
       _22, _23, _24, _25, _26, _27, _28, _29, _30, _31;

  Multiplexer #(.select(5), .width(32)) multiplexer_1 (
    .in0({32{1'b0}}), .in1(_1), .in2(_2), .in3(_3), .in4(_4), .in5(_5), .in6(_6), .in7(_7), .in8(_8),
    .in9(_9), .in10(_10), .in11(_11), .in12(_12), .in13(_13), .in14(_14), .in15(_15), .in16(_16), .in17(_17),
    .in18(_18), .in19(_19), .in20(_20), .in21(_21), .in22(_22), .in23(_23), .in24(_24), .in25(_25),
    .in26(_26), .in27(_27), .in28(_28), .in29(_29), .in30(_30), .in31(_31), .out(RD1), .sel(A1));  // open: en
  Multiplexer #(.select(5), .width(32)) multiplexer_2 (
    .in0({32{1'b0}}), .in1(_1), .in2(_2), .in3(_3), .in4(_4), .in5(_5), .in6(_6), .in7(_7), .in8(_8),
    .in9(_9), .in10(_10), .in11(_11), .in12(_12), .in13(_13), .in14(_14), .in15(_15), .in16(_16), .in17(_17),
    .in18(_18), .in19(_19), .in20(_20), .in21(_21), .in22(_22), .in23(_23), .in24(_24), .in25(_25),
    .in26(_26), .in27(_27), .in28(_28), .in29(_29), .in30(_30), .in31(_31), .out(RD2), .sel(A2));  // open: en
  assign and_1_out = A3 & {5{WE}};  // AND_Gate and_1, 5 bits wide
  Decoder #(.select(5)) decoder_1 (
    .out1(en1), .out2(en2), .out3(en3), .out4(en4), .out5(en5), .out6(en6), .out7(en7), .out8(en8),
    .out9(en9), .out10(en10), .out11(en11), .out12(en12), .out13(en13), .out14(en14), .out15(en15),
    .out16(en16), .out17(en17), .out18(en18), .out19(en19), .out20(en20), .out21(en21), .out22(en22),
    .out23(en23), .out24(en24), .out25(en25), .out26(en26), .out27(en27), .out28(en28), .out29(en29),
    .out30(en30), .out31(en31), .sel(and_1_out));  // open: out0, en
  // Probe on _1
  Register #(.width(32)) u__1 (.D(WD), .en(en1), .Q(_1), .clk(clk), .clr(reset));
  // Probe on _5
  Register #(.width(32)) u__5 (.D(WD), .en(en5), .Q(_5), .clk(clk), .clr(reset));
  // Probe on _9
  Register #(.width(32)) u__9 (.D(WD), .en(en9), .Q(_9), .clk(clk), .clr(reset));
  // Probe on _13
  Register #(.width(32)) u__13 (.D(WD), .en(en13), .Q(_13), .clk(clk), .clr(reset));
  // Probe on _2
  Register #(.width(32)) u__2 (.D(WD), .en(en2), .Q(_2), .clk(clk), .clr(reset));
  // Probe on _6
  Register #(.width(32)) u__6 (.D(WD), .en(en6), .Q(_6), .clk(clk), .clr(reset));
  // Probe on _10
  Register #(.width(32)) u__10 (.D(WD), .en(en10), .Q(_10), .clk(clk), .clr(reset));
  // Probe on _14
  Register #(.width(32)) u__14 (.D(WD), .en(en14), .Q(_14), .clk(clk), .clr(reset));
  // Probe on _3
  Register #(.width(32)) u__3 (.D(WD), .en(en3), .Q(_3), .clk(clk), .clr(reset));
  // Probe on _7
  Register #(.width(32)) u__7 (.D(WD), .en(en7), .Q(_7), .clk(clk), .clr(reset));
  // Probe on _11
  Register #(.width(32)) u__11 (.D(WD), .en(en11), .Q(_11), .clk(clk), .clr(reset));
  // Probe on _15
  Register #(.width(32)) u__15 (.D(WD), .en(en15), .Q(_15), .clk(clk), .clr(reset));
  // Probe on _4
  Register #(.width(32)) u__4 (.D(WD), .en(en4), .Q(_4), .clk(clk), .clr(reset));
  // Probe on _8
  Register #(.width(32)) u__8 (.D(WD), .en(en8), .Q(_8), .clk(clk), .clr(reset));
  // Probe on _12
  Register #(.width(32)) u__12 (.D(WD), .en(en12), .Q(_12), .clk(clk), .clr(reset));
  // Probe on _16
  Register #(.width(32)) u__16 (.D(WD), .en(en16), .Q(_16), .clk(clk), .clr(reset));
  // Probe on _17
  Register #(.width(32)) u__17 (.D(WD), .en(en17), .Q(_17), .clk(clk), .clr(reset));
  // Probe on _21
  Register #(.width(32)) u__21 (.D(WD), .en(en21), .Q(_21), .clk(clk), .clr(reset));
  // Probe on _25
  Register #(.width(32)) u__25 (.D(WD), .en(en25), .Q(_25), .clk(clk), .clr(reset));
  // Probe on _29
  Register #(.width(32)) u__29 (.D(WD), .en(en29), .Q(_29), .clk(clk), .clr(reset));
  // Probe on _18
  Register #(.width(32)) u__18 (.D(WD), .en(en18), .Q(_18), .clk(clk), .clr(reset));
  // Probe on _22
  Register #(.width(32)) u__22 (.D(WD), .en(en22), .Q(_22), .clk(clk), .clr(reset));
  // Probe on _26
  Register #(.width(32)) u__26 (.D(WD), .en(en26), .Q(_26), .clk(clk), .clr(reset));
  // Probe on _30
  Register #(.width(32)) u__30 (.D(WD), .en(en30), .Q(_30), .clk(clk), .clr(reset));
  // Probe on _19
  Register #(.width(32)) u__19 (.D(WD), .en(en19), .Q(_19), .clk(clk), .clr(reset));
  // Probe on _23
  Register #(.width(32)) u__23 (.D(WD), .en(en23), .Q(_23), .clk(clk), .clr(reset));
  // Probe on _27
  Register #(.width(32)) u__27 (.D(WD), .en(en27), .Q(_27), .clk(clk), .clr(reset));
  // Probe on _31
  Register #(.width(32)) u__31 (.D(WD), .en(en31), .Q(_31), .clk(clk), .clr(reset));
  // Probe on _20
  Register #(.width(32)) u__20 (.D(WD), .en(en20), .Q(_20), .clk(clk), .clr(reset));
  // Probe on _24
  Register #(.width(32)) u__24 (.D(WD), .en(en24), .Q(_24), .clk(clk), .clr(reset));
  // Probe on _28
  Register #(.width(32)) u__28 (.D(WD), .en(en28), .Q(_28), .clk(clk), .clr(reset));

  // Other names for the same wires on the sheet: en = WE; A1_slt[31:0] = RD1; A2_slt[31:0] = RD2; rst = reset;
  //   word[31:0] = WD

  // Notes on the sheet:
  //   Read   lw RD1, $A1
  //   Read   lw RD2, $A2
  //   Write   sw WD, $A3
  //   $at
  //   $a1
  //   $t1
  //   $t5
  //   General Register File ($0 ~ $31)
  //   $v0
  //   $a2
  //   $t2
  //   $t6
  //   $v1
  //   $a3
  //   $t3
  //   $t7
  //   $a0
  //   $t0
  //   $t4
  //   $s0
  //   $zero
  //   $s1
  //   $s5
  //   $t9
  //   $sp
  //   $s2
  //   $s6
  //   $k0
  //   $fp
  //   $s3
  //   $s7
  //   $k1
  //   $ra
  //   $s4
  //   $t8
  //   $gp
endmodule
