// Logisim project RegularExpression_simple.circ as structural Verilog: 3 circuits, main circuit output_translator
module fsm (
  input  CLR,
  input  [1:0] In,
  output Z
);

  wire clock_1_out;
  wire [1:0] multiplexer_1_out, register_1_q, trans_1_new;

  trans trans_1 (.Rout(register_1_q), .In(In), .New(trans_1_new));
  Multiplexer #(.width(2)) multiplexer_1 (
    .in0(trans_1_new), .in1(2'b00), .out(multiplexer_1_out), .sel(CLR));  // open: en
  Register #(.width(2)) register_1 (.D(multiplexer_1_out), .Q(register_1_q), .clk(clock_1_out));  // open: en, clr
  Clock clock_1 (.out(clock_1_out));
  output_translator output_translator_1 (.In(In), .Rout(register_1_q), .Out(Z));

  // Other names for the same wires on the sheet: aaaaaaaaaaa[1:0] = In

  // Notes on the sheet:
  //   In: 00 for 'a'; 01 for 'b'; 10 for 'c'; 11 for others.
  //   Mealy FSM for Regular Expression "b{1,2}[ac]{2}"
endmodule

module output_translator (
  input  [1:0] In,
  input  [1:0] Rout,
  output Out
);

  wire not_1_out;

  not not_1 (not_1_out, In[0]);
  and and_1 (Out, not_1_out, Rout[1], Rout[0]);

  // Notes on the sheet:
  //   Output = 1 only when state==3 && in=='a/c'
endmodule

// state trans
module trans (
  input  [1:0] Rout,
  input  [1:0] In,
  output [1:0] New
);

  wire and_1_out, and_2_out, and_3_out, and_4_out, and_5_out, and_6_out, and_7_out, and_8_out, not_1_out,
       not_2_out, not_3_out, not_4_out, not_5_out, not_6_out, not_7_out, not_8_out, not_9_out, not_10_out,
       not_11_out, not_12_out, not_13_out, not_14_out, not_15_out, not_16_out;

  not not_1 (not_1_out, Rout[1]);
  not not_2 (not_2_out, In[1]);
  not not_3 (not_3_out, Rout[1]);
  not not_4 (not_4_out, In[0]);
  not not_5 (not_5_out, Rout[0]);
  not not_6 (not_6_out, In[1]);
  not not_7 (not_7_out, Rout[0]);
  not not_8 (not_8_out, In[0]);
  not not_9 (not_9_out, Rout[1]);
  not not_10 (not_10_out, Rout[0]);
  not not_11 (not_11_out, In[1]);
  not not_12 (not_12_out, Rout[1]);
  not not_13 (not_13_out, In[0]);
  not not_14 (not_14_out, Rout[0]);
  not not_15 (not_15_out, In[0]);
  not not_16 (not_16_out, In[1]);
  and and_1 (and_1_out, not_1_out, Rout[0], not_2_out);
  and and_2 (and_2_out, not_3_out, Rout[0], not_4_out);
  and and_3 (and_3_out, Rout[1], not_5_out, not_6_out);
  and and_4 (and_4_out, Rout[1], not_7_out, not_8_out);
  and and_5 (and_5_out, not_9_out, not_10_out, not_11_out, In[0]);
  and and_6 (and_6_out, not_12_out, Rout[0], not_13_out);
  and and_7 (and_7_out, Rout[1], not_14_out, not_15_out);
  and and_8 (and_8_out, Rout[1], Rout[0], not_16_out, In[0]);
  or or_1 (New[1], and_1_out, and_2_out, and_3_out, and_4_out);
  or or_2 (New[0], and_5_out, and_6_out, and_7_out, and_8_out);
endmodule
