// Logisim project SingleCycle.circ as structural Verilog: 11 circuits, main circuit main
module main (
  input  Reset,
  output [31:0] Instr
);

  wire ALU_zero, Branch, clock_1_out, clock_2_out, jump, Link, MemtoReg, MemWrite, RegDst, RegWrite;
  wire [0:0] PC_choice;
  wire [1:0] ALUSrc;
  wire [2:0] ALUControl;
  wire [4:0] lw_sw_5bits_addr_out_2, multiplexer_1_out, multiplexer_2_out;
  wire [5:0] opcode;
  wire [25:0] addr;
  wire [31:0] ALU_aluresult, ImmCalc_left16_imm32, ImmCalc_zero_imm32, multiplexer_3_out, multiplexer_4_out,
       PC_4, ram_1_data, RegFile_rd1, RegFile_rd2, result, sign_imm32;

  Instr_Fetcher_signed32__PCmux__Reset__Instr__Ins_split InstrFetcher (
    .sign_imm32(sign_imm32), .addr26(addr), .PC_choice({jump, PC_choice[0]}), .GlobalReset(Reset),
    .funct(addr[5:0]), .shamt(addr[10:6]), .rd(addr[15:11]), .rt(addr[20:16]), .rs(addr[25:21]),
    .opcode(opcode), .Instr(Instr));
  Multiplexer #(.width(5)) multiplexer_1 (
    .in0(addr[20:16]), .in1(addr[15:11]), .out(multiplexer_1_out), .sel(RegDst));  // open: en
  Multiplexer #(.width(5)) multiplexer_2 (
    .in0(multiplexer_1_out), .in1({5{1'b1}}), .out(multiplexer_2_out), .sel(Link));  // open: en
  Multiplexer #(.width(32)) multiplexer_3 (.in0(result), .in1(PC_4), .out(multiplexer_3_out), .sel(Link));  // open: en
  Controller_op__funct__7sig Controller (
    .opcode(opcode), .funct(addr[5:0]), .MemtoReg(MemtoReg), .MemWrite(MemWrite), .Branch(Branch),
    .ALUControl(ALUControl), .ALUSrc(ALUSrc), .RegDst(RegDst), .RegWrite(RegWrite), .Jump(jump));
  Clock clock_1 (.out(clock_1_out));
  General_Register_File RegFile (
    .A1(addr[25:21]), .A2(addr[20:16]), .A3(multiplexer_2_out), .WD(multiplexer_3_out), .clk(clock_1_out),
    .reset(Reset), .WE(RegWrite), .RD1(RegFile_rd1), .RD2(RegFile_rd2));
  Imm_Calculator ImmCalc (
    .imm16(addr[15:0]), .sign_imm32(sign_imm32), .zero_imm32(ImmCalc_zero_imm32),
    .left16_imm32(ImmCalc_left16_imm32));
  Multiplexer #(.select(2), .width(32)) multiplexer_4 (
    .in0(RegFile_rd2), .in1(sign_imm32), .in2(ImmCalc_zero_imm32), .in3(ImmCalc_left16_imm32),
    .out(multiplexer_4_out), .sel(ALUSrc));  // open: en
  ALU_A__B__ALUControl__C ALU (
    .A(RegFile_rd1), .B(multiplexer_4_out), .ALUControl(ALUControl), .Zero(ALU_zero),
    .ALUResult(ALU_aluresult));
  and u_PC_Choice (PC_choice[0], Branch, ALU_zero);
  AddrRes_To_Mem_ALURes__addr lw_sw_5bits_addr (.in_1(ALU_aluresult), .out_2(lw_sw_5bits_addr_out_2));
  // Probe on RegFile_rd2
  Clock clock_2 (.out(clock_2_out));
  Multiplexer #(.width(32)) multiplexer_5 (
    .in0(ALU_aluresult), .in1(ram_1_data), .out(result), .sel(MemtoReg));  // open: en
  RAM #(.addrWidth(5), .dataWidth(32), .bus("separate")) ram_1 (
    .addr(lw_sw_5bits_addr_out_2), .din(RegFile_rd2), .data(ram_1_data), .str(MemWrite), .clk(clock_2_out),
    .clr(Reset));  // open: sel, ld
  // Probe on ram_1_data
  // Probe on result

  // Other names for the same wires on the sheet: func[5:0] = addr[5:0]; imm[15:0] = addr[15:0];
  //   shamt[4:0] = addr[10:6]; rd[4:0] = addr[15:11]; rt[4:0] = addr[20:16]; rs[4:0] = addr[25:21];
  //   GlobalReset = Reset; PC_choice[1] = jump

  // Notes on the sheet:
  //   R Instr
  //   I Instr
  //   J Instr
endmodule

module Controller_op__funct__7sig (
  input  [5:0] opcode,
  input  [5:0] funct,
  output MemtoReg,
  output MemWrite,
  output Branch,
  output [2:0] ALUControl,
  output [1:0] ALUSrc,
  output RegDst,
  output RegWrite,
  output Jump
);

  wire and_1_out, and_2_out, and_3_out, and_4_out, and_5_out, and_6_out, and_7_out, and_8_out, and_9_out,
       and_10_out, and_11_out, and_12_out, and_13_out, not_1_out, not_2_out, not_3_out, not_4_out, not_5_out,
       not_6_out, not_7_out, not_8_out, not_9_out, not_10_out, not_11_out, not_12_out;
  wire [2:0] and_21_out, and_22_out, and_23_out, and_24_out, and_25_out, and_26_out, bit_extender_8_out,
       bit_extender_9_out, bit_extender_10_out, bit_extender_11_out, bit_extender_12_out,
       bit_extender_13_out, R_ALUControl;
  wire [10:0] and_14_out, and_15_out, and_16_out, and_17_out, and_18_out, and_19_out, and_20_out,
       bit_extender_1_out, bit_extender_2_out, bit_extender_3_out, bit_extender_4_out, bit_extender_5_out,
       bit_extender_6_out, bit_extender_7_out;

  not not_1 (not_1_out, opcode[5]);
  not not_2 (not_2_out, opcode[4]);
  not not_3 (not_3_out, funct[5]);
  not not_4 (not_4_out, opcode[2]);
  not not_5 (not_5_out, opcode[3]);
  not not_6 (not_6_out, funct[3]);
  not not_7 (not_7_out, funct[4]);
  not not_8 (not_8_out, opcode[0]);
  not not_9 (not_9_out, opcode[1]);
  not not_10 (not_10_out, funct[2]);
  not not_11 (not_11_out, funct[1]);
  and and_1 (and_1_out, opcode[5], not_2_out, not_5_out, not_4_out, opcode[1], opcode[0]);
  and and_2 (and_2_out, opcode[5], not_2_out, opcode[3], not_4_out, opcode[1], opcode[0]);
  and and_3 (and_3_out, not_1_out, not_2_out, not_5_out, not_4_out, not_9_out, not_8_out);
  and and_4 (and_4_out, not_1_out, not_2_out, not_5_out, opcode[2], not_9_out, not_8_out);
  and and_5 (and_5_out, not_1_out, not_2_out, opcode[3], opcode[2], not_9_out, opcode[0]);
  and and_6 (and_6_out, not_1_out, not_2_out, opcode[3], opcode[2], opcode[1], opcode[0]);
  and and_7 (and_7_out, not_1_out, not_2_out, not_5_out, not_4_out, opcode[1], not_8_out);
  not not_12 (not_12_out, funct[0]);
  and and_8 (and_8_out, funct[5], not_7_out, not_6_out, not_10_out, not_11_out, funct[0]);
  and and_9 (and_9_out, funct[5], not_7_out, not_6_out, not_10_out, funct[1], funct[0]);
  and and_10 (and_10_out, funct[5], not_7_out, not_6_out, funct[2], not_11_out, not_12_out);
  and and_11 (and_11_out, funct[5], not_7_out, not_6_out, funct[2], not_11_out, funct[0]);
  and and_12 (and_12_out, funct[5], not_7_out, funct[3], not_10_out, funct[1], not_12_out);
  and and_13 (and_13_out, not_3_out, not_7_out, not_6_out, not_10_out, not_11_out, not_12_out);
  assign bit_extender_1_out = {{10{and_1_out}}, and_1_out};  // Bit_Extender bit_extender_1
  assign bit_extender_2_out = {{10{and_2_out}}, and_2_out};  // Bit_Extender bit_extender_2
  assign bit_extender_3_out = {{10{and_3_out}}, and_3_out};  // Bit_Extender bit_extender_3
  assign bit_extender_4_out = {{10{and_4_out}}, and_4_out};  // Bit_Extender bit_extender_4
  assign bit_extender_5_out = {{10{and_5_out}}, and_5_out};  // Bit_Extender bit_extender_5
  assign bit_extender_6_out = {{10{and_6_out}}, and_6_out};  // Bit_Extender bit_extender_6
  assign bit_extender_7_out = {{10{and_7_out}}, and_7_out};  // Bit_Extender bit_extender_7
  assign and_14_out = bit_extender_1_out & 11'h44a;  // AND_Gate and_14, 11 bits wide
  assign and_15_out = bit_extender_2_out & 11'h248;  // AND_Gate and_15, 11 bits wide
  assign and_16_out = bit_extender_3_out & {3'b000, R_ALUControl, 5'b00110};  // AND_Gate and_16, 11 bits wide
  assign and_17_out = bit_extender_4_out & 11'h1c0;  // AND_Gate and_17, 11 bits wide
  assign and_18_out = bit_extender_5_out & 11'h32;  // AND_Gate and_18, 11 bits wide
  assign and_19_out = bit_extender_6_out & 11'h5a;  // AND_Gate and_19, 11 bits wide
  assign and_20_out = bit_extender_7_out & 11'h1;  // AND_Gate and_20, 11 bits wide
  assign bit_extender_8_out = {{2{and_8_out}}, and_8_out};  // Bit_Extender bit_extender_8
  assign and_21_out = bit_extender_8_out & 3'b010;  // AND_Gate and_21, 3 bits wide
  assign bit_extender_9_out = {{2{and_9_out}}, and_9_out};  // Bit_Extender bit_extender_9
  assign and_22_out = bit_extender_9_out & 3'b110;  // AND_Gate and_22, 3 bits wide
  assign bit_extender_10_out = {{2{and_10_out}}, and_10_out};  // Bit_Extender bit_extender_10
  assign and_23_out = bit_extender_10_out & 3'b000;  // AND_Gate and_23, 3 bits wide
  assign bit_extender_11_out = {{2{and_11_out}}, and_11_out};  // Bit_Extender bit_extender_11
  assign and_24_out = bit_extender_11_out & 3'b001;  // AND_Gate and_24, 3 bits wide
  assign bit_extender_12_out = {{2{and_12_out}}, and_12_out};  // Bit_Extender bit_extender_12
  assign and_25_out = bit_extender_12_out & 3'b111;  // AND_Gate and_25, 3 bits wide
  assign bit_extender_13_out = {{2{and_13_out}}, and_13_out};  // Bit_Extender bit_extender_13
  assign and_26_out = bit_extender_13_out & 3'b000;  // AND_Gate and_26, 3 bits wide
  assign {MemtoReg, MemWrite, Branch, ALUControl, ALUSrc, RegDst, RegWrite, Jump} = and_14_out | and_15_out | and_16_out | and_17_out | and_18_out | and_19_out | and_20_out;  // OR_Gate or_1, 11 bits wide
  assign R_ALUControl = and_21_out | and_22_out | and_23_out | and_24_out | and_25_out | and_26_out;  // OR_Gate or_2, 3 bits wide

  // Notes on the sheet:
  //   lw: 100011
  //   sw: 101011
  //   R: 000000, considering funct
  //   beq: 000100
  //   ori: 001101
  //   lui: 001111
  //   j: 000010
  //   addU: 100001
  //   subU: 100011
  //   and: 100100
  //   or: 100101
  //   slt: 101010
  //   nop: 000000
endmodule

module ALU_A__B__ALUControl__C (
  input  [2:0] ALUControl,
  input  [31:0] A,
  input  [31:0] B,
  output Zero,
  output [31:0] ALUResult
);

  wire comparator_1_lt;
  wire [31:0] adder_1_out, and_1_out, bit_extender_1_out, or_1_out, subtractor_1_out;

  Adder #(.width(32)) adder_1 (.a(A), .b(B), .out(adder_1_out));  // open: cin, cout
  Subtractor #(.width(32)) subtractor_1 (.a(A), .b(B), .out(subtractor_1_out));  // open: bin, bout
  assign and_1_out = A & B;  // AND_Gate and_1, 32 bits wide
  assign or_1_out = A | B;  // OR_Gate or_1, 32 bits wide
  Comparator #(.width(32), .mode("unsigned")) comparator_1 (.a(A), .b(B), .lt(comparator_1_lt));  // open: gt, eq
  assign bit_extender_1_out = {{31{1'b0}}, comparator_1_lt};  // Bit_Extender bit_extender_1
  Multiplexer #(.select(3), .width(32)) multiplexer_1 (
    .in0(and_1_out), .in1(or_1_out), .in2(adder_1_out), .in6(subtractor_1_out), .in7(bit_extender_1_out),
    .out(ALUResult), .sel(ALUControl));  // open: in3, in4, in5, en
  Comparator #(.width(32), .mode("unsigned")) comparator_2 (.a({32{1'b0}}), .b(ALUResult), .eq(Zero));  // open: gt, lt
endmodule

module AddrRes_To_Mem_ALURes__addr (
  input  [31:0] in_1,
  output [4:0] out_2
);

  wire [31:5] shifter_1_out;

  Shifter #(.width(32), .shift("lr")) shifter_1 (.in(in_1), .\dist (5'b00010), .out({shifter_1_out, out_2}));
endmodule

module PC_4_oldPC__NewPC (
  input  [31:0] OldPc,
  output [31:0] NewPc
);

  Adder #(.width(32)) adder_1 (.a(OldPc), .b(32'h4), .out(NewPc));  // open: cin, cout
endmodule

module PC_4_Imm_4_oldPC__Imm32__NewPC (
  input  [31:0] Imm32,
  input  [31:0] old_PC,
  output [31:0] new_PC
);

  wire [31:0] pc_4_oldpc_newpc_1_newpc, shifter_1_out;

  Shifter #(.width(32)) shifter_1 (.in(Imm32), .\dist (5'b00010), .out(shifter_1_out));
  PC_4_oldPC__NewPC pc_4_oldpc_newpc_1 (.OldPc(old_PC), .NewPc(pc_4_oldpc_newpc_1_newpc));
  Adder #(.width(32)) adder_1 (.a(shifter_1_out), .b(pc_4_oldpc_newpc_1_newpc), .out(new_PC));  // open: cin, cout
endmodule

module NextPC_oldPC__Imm32__PCmux__NewPC (
  input  [31:0] oldPC,
  input  [31:0] Imm32,
  input  [25:0] addr26,
  input  [1:0] PC_mux,
  output [31:0] out_5
);

  wire [31:0] Branch_PC_Calc_new_pc, Jump_PC_Calc_new_pc, Normal_PC_Calc_newpc;

  // Probe on oldPC
  // Probe on Imm32
  // Probe on addr26
  PC_4_oldPC__NewPC Normal_PC_Calc (.OldPc(oldPC), .NewPc(Normal_PC_Calc_newpc));
  PC_4_Imm_4_oldPC__Imm32__NewPC Branch_PC_Calc (.Imm32(Imm32), .old_PC(oldPC), .new_PC(Branch_PC_Calc_new_pc));
  PC4_Addr_00_oldPC__addr26__NewPC Jump_PC_Calc (.addr26(addr26), .old_PC(oldPC), .new_PC(Jump_PC_Calc_new_pc));
  // Probe on out_5
  Multiplexer #(.select(2), .width(32)) multiplexer_1 (
    .in0(Normal_PC_Calc_newpc), .in1(Branch_PC_Calc_new_pc), .in2(Jump_PC_Calc_new_pc), .out(out_5),
    .sel(PC_mux));  // open: in3, en
endmodule

module Instr_Fetcher_signed32__PCmux__Reset__Instr__Ins_split (
  input  [31:0] sign_imm32,
  input  [25:0] addr26,
  input  [1:0] PC_choice,
  input  GlobalReset,
  output [5:0] funct,
  output [4:0] shamt,
  output [4:0] rd,
  output [4:0] rt,
  output [4:0] rs,
  output [5:0] opcode,
  output [31:0] Instr
);

  wire clock_1_out;
  wire [31:0] NextPC_out_5, PC_q;

  NextPC_oldPC__Imm32__PCmux__NewPC NextPC (
    .oldPC(PC_q), .Imm32(sign_imm32), .addr26(addr26), .PC_mux(PC_choice), .out_5(NextPC_out_5));
  Register #(.width(32)) PC (.D(NextPC_out_5), .Q(PC_q), .clk(clock_1_out), .clr(GlobalReset));  // open: en
  Clock clock_1 (.out(clock_1_out));
  // Probe on {Instr[31:6], funct}
  ROM #(.addrWidth(5), .dataWidth(32)) rom_1 (.addr(PC_q[6:2]), .data({Instr[31:6], funct}));  // open: sel

  assign Instr[5:0] = funct;
  assign opcode = Instr[31:26];
  assign rd = Instr[15:11];
  assign rs = Instr[25:21];
  assign rt = Instr[20:16];
  assign shamt = Instr[10:6];

  // Notes on the sheet:
  //   R Instr
endmodule

module Imm_Calculator (
  input  [15:0] imm16,
  output [31:0] sign_imm32,
  output [31:0] zero_imm32,
  output [31:0] left16_imm32
);

  assign sign_imm32 = {{16{imm16[15]}}, imm16};  // Bit_Extender bit_extender_1
  assign zero_imm32 = {{16{1'b0}}, imm16};  // Bit_Extender bit_extender_2

  assign left16_imm32 = {imm16, {16{1'b0}}};
endmodule

module General_Register_File (
  input  clk,
  input  reset,
  input  WE,
  input  [4:0] A1,
  input  [4:0] A2,
  input  [4:0] A3,
  input  [31:0] WD,
  output [31:0] RD1,
  output [31:0] RD2
);

  wire en1, en2, en3, en4, en5, en6, en7, en8, en9, en10, en11, en12, en13, en14, en15, en16, en17, en18,
       en19, en20, en21, en22, en23, en24, en25, en26, en27, en28, en29, en30, en31;
  wire [4:0] and_1_out;
  wire [31:0] _1, _2, _3, _4, _5, _6, _7, _8, _9, _10, _11, _12, _13, _14, _15, _16, _17, _18, _19, _20, _21,
       _22, _23, _24, _25, _26, _27, _28, _29, _30, _31;

  Multiplexer #(.select(5), .width(32)) multiplexer_1 (
    .in0({32{1'b0}}), .in1(_1), .in2(_2), .in3(_3), .in4(_4), .in5(_5), .in6(_6), .in7(_7), .in8(_8),
    .in9(_9), .in10(_10), .in11(_11), .in12(_12), .in13(_13), .in14(_14), .in15(_15), .in16(_16), .in17(_17),
    .in18(_18), .in19(_19), .in20(_20), .in21(_21), .in22(_22), .in23(_23), .in24(_24), .in25(_25),
    .in26(_26), .in27(_27), .in28(_28), .in29(_29), .in30(_30), .in31(_31), .out(RD1), .sel(A1));  // open: en
  Multiplexer #(.select(5), .width(32)) multiplexer_2 (
    .in0({32{1'b0}}), .in1(_1), .in2(_2), .in3(_3), .in4(_4), .in5(_5), .in6(_6), .in7(_7), .in8(_8),
    .in9(_9), .in10(_10), .in11(_11), .in12(_12), .in13(_13), .in14(_14), .in15(_15), .in16(_16), .in17(_17),
    .in18(_18), .in19(_19), .in20(_20), .in21(_21), .in22(_22), .in23(_23), .in24(_24), .in25(_25),
    .in26(_26), .in27(_27), .in28(_28), .in29(_29), .in30(_30), .in31(_31), .out(RD2), .sel(A2));  // open: en
  assign and_1_out = A3 & {5{WE}};  // AND_Gate and_1, 5 bits wide
  Decoder #(.select(5)) decoder_1 (
    .out1(en1), .out2(en2), .out3(en3), .out4(en4), .out5(en5), .out6(en6), .out7(en7), .out8(en8),
    .out9(en9), .out10(en10), .out11(en11), .out12(en12), .out13(en13), .out14(en14), .out15(en15),
    .out16(en16), .out17(en17), .out18(en18), .out19(en19), .out20(en20), .out21(en21), .out22(en22),
    .out23(en23), .out24(en24), .out25(en25), .out26(en26), .out27(en27), .out28(en28), .out29(en29),
    .out30(en30), .out31(en31), .sel(and_1_out));  // open: out0, en
  // Probe on _1
  Register #(.width(32)) u__1 (.D(WD), .en(en1), .Q(_1), .clk(clk), .clr(reset));
  // Probe on _5
  Register #(.width(32)) u__5 (.D(WD), .en(en5), .Q(_5), .clk(clk), .clr(reset));
  // Probe on _9
  Register #(.width(32)) u__9 (.D(WD), .en(en9), .Q(_9), .clk(clk), .clr(reset));
  // Probe on _13
  Register #(.width(32)) u__13 (.D(WD), .en(en13), .Q(_13), .clk(clk), .clr(reset));
  // Probe on _2
  Register #(.width(32)) u__2 (.D(WD), .en(en2), .Q(_2), .clk(clk), .clr(reset));
  // Probe on _6
  Register #(.width(32)) u__6 (.D(WD), .en(en6), .Q(_6), .clk(clk), .clr(reset));
  // Probe on _10
  Register #(.width(32)) u__10 (.D(WD), .en(en10), .Q(_10), .clk(clk), .clr(reset));
  // Probe on _14
  Register #(.width(32)) u__14 (.D(WD), .en(en14), .Q(_14), .clk(clk), .clr(reset));
  // Probe on _3
  Register #(.width(32)) u__3 (.D(WD), .en(en3), .Q(_3), .clk(clk), .clr(reset));
  // Probe on _7
  Register #(.width(32)) u__7 (.D(WD), .en(en7), .Q(_7), .clk(clk), .clr(reset));
  // Probe on _11
  Register #(.width(32)) u__11 (.D(WD), .en(en11), .Q(_11), .clk(clk), .clr(reset));
  // Probe on _15
  Register #(.width(32)) u__15 (.D(WD), .en(en15), .Q(_15), .clk(clk), .clr(reset));
  // Probe on _4
  Register #(.width(32)) u__4 (.D(WD), .en(en4), .Q(_4), .clk(clk), .clr(reset));
  // Probe on _8
  Register #(.width(32)) u__8 (.D(WD), .en(en8), .Q(_8), .clk(clk), .clr(reset));
  // Probe on _12
  Register #(.width(32)) u__12 (.D(WD), .en(en12), .Q(_12), .clk(clk), .clr(reset));
  // Probe on _16
  Register #(.width(32)) u__16 (.D(WD), .en(en16), .Q(_16), .clk(clk), .clr(reset));
  // Probe on _17
  Register #(.width(32)) u__17 (.D(WD), .en(en17), .Q(_17), .clk(clk), .clr(reset));
  // Probe on _21
  Register #(.width(32)) u__21 (.D(WD), .en(en21), .Q(_21), .clk(clk), .clr(reset));
  // Probe on _25
  Register #(.width(32)) u__25 (.D(WD), .en(en25), .Q(_25), .clk(clk), .clr(reset));
  // Probe on _29
  Register #(.width(32)) u__29 (.D(WD), .en(en29), .Q(_29), .clk(clk), .clr(reset));
  // Probe on _18
  Register #(.width(32)) u__18 (.D(WD), .en(en18), .Q(_18), .clk(clk), .clr(reset));
  // Probe on _22
  Register #(.width(32)) u__22 (.D(WD), .en(en22), .Q(_22), .clk(clk), .clr(reset));
  // Probe on _26
  Register #(.width(32)) u__26 (.D(WD), .en(en26), .Q(_26), .clk(clk), .clr(reset));
  // Probe on _30
  Register #(.width(32)) u__30 (.D(WD), .en(en30), .Q(_30), .clk(clk), .clr(reset));
  // Probe on _19
  Register #(.width(32)) u__19 (.D(WD), .en(en19), .Q(_19), .clk(clk), .clr(reset));
  // Probe on _23
  Register #(.width(32)) u__23 (.D(WD), .en(en23), .Q(_23), .clk(clk), .clr(reset));
  // Probe on _27
  Register #(.width(32)) u__27 (.D(WD), .en(en27), .Q(_27), .clk(clk), .clr(reset));
  // Probe on _31
  Register #(.width(32)) u__31 (.D(WD), .en(en31), .Q(_31), .clk(clk), .clr(reset));
  // Probe on _20
  Register #(.width(32)) u__20 (.D(WD), .en(en20), .Q(_20), .clk(clk), .clr(reset));
  // Probe on _24
  Register #(.width(32)) u__24 (.D(WD), .en(en24), .Q(_24), .clk(clk), .clr(reset));
  // Probe on _28
  Register #(.width(32)) u__28 (.D(WD), .en(en28), .Q(_28), .clk(clk), .clr(reset));

  // Other names for the same wires on the sheet: en = WE; A1_slt[31:0] = RD1; A2_slt[31:0] = RD2; rst = reset;
  //   word[31:0] = WD

  // Notes on the sheet:
  //   Read   lw RD1, $A1
  //   Read   lw RD2, $A2
  //   Write   sw WD, $A3
  //   $at
  //   $a1
  //   $t1
  //   $t5
  //   General Register File ($0 ~ $31)
  //   $v0
  //   $a2
  //   $t2
  //   $t6
  //   $v1
  //   $a3
  //   $t3
  //   $t7
  //   $a0
  //   $t0
  //   $t4
  //   $s0
  //   $zero
  //   $s1
  //   $s5
  //   $t9
  //   $sp
  //   $s2
  //   $s6
  //   $k0
  //   $fp
  //   $s3
  //   $s7
  //   $k1
  //   $ra
  //   $s4
  //   $t8
  //   $gp
endmodule

module PC4_Addr_00_oldPC__addr26__NewPC (
  input  [25:0] addr26,
  input  [31:0] old_PC,
  output [31:0] new_PC
);

  wire [27:0] pc_4_oldpc_newpc_1_newpc;

  PC_4_oldPC__NewPC pc_4_oldpc_newpc_1 (.OldPc(old_PC), .NewPc({new_PC[31:28], pc_4_oldpc_newpc_1_newpc}));

  assign new_PC[27:0] = {addr26, 2'b00};
endmodule
