// Logisim project 2pown_mod_5.circ as structural Verilog: 4 circuits, main circuit Transition
module Transition (
  input  [4:0] Prev,
  input  \input ,
  output [4:0] \output 
);

  Trans trans_1 (
    .p0(Prev[4]), .p1(Prev[3]), .p2(Prev[2]), .p3(Prev[1]), .p4(Prev[0]), .in(\input ), .o0(\output [4]),
    .o1(\output [3]), .o2(\output [2]), .o3(\output [1]), .o4(\output [0]));
endmodule

module Trans (
  input  p0,
  input  p1,
  input  p2,
  input  p3,
  input  p4,
  input  in,
  output o0,
  output o1,
  output o2,
  output o3,
  output o4
);

  wire not_1_out, not_2_out, not_3_out, not_4_out, not_5_out, not_6_out, not_7_out, not_8_out, not_9_out,
       not_10_out, not_11_out, not_12_out, not_13_out, not_14_out;

  not not_1 (not_1_out, p0);
  not not_2 (not_2_out, p2);
  not not_3 (not_3_out, p3);
  not not_4 (not_4_out, in);
  not not_5 (not_5_out, p0);
  not not_6 (not_6_out, p2);
  not not_7 (not_7_out, p3);
  not not_8 (not_8_out, p0);
  not not_9 (not_9_out, p1);
  not not_10 (not_10_out, p4);
  not not_11 (not_11_out, p0);
  not not_12 (not_12_out, p1);
  not not_13 (not_13_out, p4);
  not not_14 (not_14_out, in);
  and and_1 (o1, not_1_out, not_2_out, not_3_out, not_4_out);
  and and_2 (o2, not_5_out, not_6_out, not_7_out, in);
  and and_3 (o3, not_8_out, not_9_out, not_10_out, in);
  and and_4 (o4, not_11_out, not_12_out, not_13_out, not_14_out);

  assign o0 = p0;
endmodule

module mod5 (
  input  In,
  output S0,
  output S1,
  output S2,
  output S3,
  output S4
);

  wire Clock_out;
  wire [4:0] Initializer_out_2, Mem_q;

  Clock Clock (.out(Clock_out));
  Initializer Initializer (.in_1(Mem_q), .out_2(Initializer_out_2));
  Register #(.width(5)) Mem (.D({S0, S1, S2, S3, S4}), .en(1'b1), .Q(Mem_q), .clk(Clock_out), .clr(1'b0));
  Transition Transitor (.Prev(Initializer_out_2), .\input (In), .\output ({S0, S1, S2, S3, S4}));

  // Notes on the sheet:
  //   Moore FSM: Transitor + Memory(Initializer) + Output + Feedback
endmodule

module Initializer (
  input  [4:0] in_1,
  output [4:0] out_2
);

  wire nor_1_out;

  Multiplexer #(.width(5)) multiplexer_1 (.in0(in_1), .in1(5'b01000), .out(out_2), .sel(nor_1_out), .en(1'b1));
  nor nor_1 (nor_1_out, in_1[0], in_1[1], in_1[2], in_1[3], in_1[4]);

  // Notes on the sheet:
  //   Initialize the Register: If(default 00000) then (set to 01000)
endmodule
