// Logisim project 4bit_swap.circ as structural Verilog: 5 circuits, main circuit 1bit_swap
module _1bit_select (
  input  I1,
  input  I2,
  input  S,
  output O
);

  wire _0__I1_out, _1__I2_out, not_1_out;

  not not_1 (not_1_out, S);
  and _0__I1 (_0__I1_out, I1, not_1_out);
  and _1__I2 (_1__I2_out, I2, S);
  or or_1 (O, _0__I1_out, _1__I2_out);
endmodule

module _1bit_swap (
  input  I1,
  input  I2,
  input  S,
  output O1,
  output O2
);

  wire not_1_out;

  _1bit_select u_1bit_select_1 (.I1(I1), .I2(I2), .S(S), .O(O1));
  not not_1 (not_1_out, S);
  _1bit_select u_1bit_select_2 (.I1(I1), .I2(I2), .S(not_1_out), .O(O2));

  // Notes on the sheet:
  //   1bit_swap: import 1bit_select
endmodule

module _4bit_swap (
  input  [3:0] I1_4bit,
  input  [3:0] I2_4bit,
  input  S,
  output [3:0] O1_4bit,
  output [3:0] O2_4bit
);

  _1bit_swap u_1bit_swap_1 (.I1(I1_4bit[0]), .I2(I2_4bit[0]), .S(S), .O1(O1_4bit[0]), .O2(O2_4bit[0]));
  _1bit_swap u_1bit_swap_2 (.I1(I1_4bit[1]), .I2(I2_4bit[1]), .S(S), .O1(O1_4bit[1]), .O2(O2_4bit[1]));
  _1bit_swap u_1bit_swap_3 (.I1(I1_4bit[2]), .I2(I2_4bit[2]), .S(S), .O1(O1_4bit[2]), .O2(O2_4bit[2]));
  _1bit_swap u_1bit_swap_4 (.I1(I1_4bit[3]), .I2(I2_4bit[3]), .S(S), .O1(O1_4bit[3]), .O2(O2_4bit[3]));

  // Notes on the sheet:
  //   4bit_swap: import 1bit_swap
endmodule

module _4bit_sort (
  input  [3:0] A,
  input  [3:0] B,
  input  [3:0] C,
  input  [3:0] D,
  output [3:0] _1,
  output [3:0] _2,
  output [3:0] _3,
  output [3:0] _4
);

  wire [3:0] n4bit_2num_sort_1_out_3, n4bit_2num_sort_1_out_4, n4bit_2num_sort_2_out_3,
       n4bit_2num_sort_2_out_4, n4bit_2num_sort_3_out_4, n4bit_2num_sort_4_out_3;

  _4bit_2num_sort u_4bit_2num_sort_1 (.A(A), .B(B), .out_3(n4bit_2num_sort_1_out_3), .out_4(n4bit_2num_sort_1_out_4));
  _4bit_2num_sort u_4bit_2num_sort_2 (.A(C), .B(D), .out_3(n4bit_2num_sort_2_out_3), .out_4(n4bit_2num_sort_2_out_4));
  _4bit_2num_sort u_4bit_2num_sort_3 (
    .A(n4bit_2num_sort_1_out_3), .B(n4bit_2num_sort_2_out_3), .out_3(_1), .out_4(n4bit_2num_sort_3_out_4));
  _4bit_2num_sort u_4bit_2num_sort_4 (
    .A(n4bit_2num_sort_2_out_4), .B(n4bit_2num_sort_1_out_4), .out_3(n4bit_2num_sort_4_out_3), .out_4(_4));
  _4bit_2num_sort u_4bit_2num_sort_5 (.A(n4bit_2num_sort_3_out_4), .B(n4bit_2num_sort_4_out_3), .out_3(_2), .out_4(_3));

  // Notes on the sheet:
  //   4bit_4num_sort: import 4bit_2num_sort
endmodule

module _4bit_2num_sort (
  input  [3:0] A,
  input  [3:0] B,
  output [3:0] out_3,
  output [3:0] out_4
);

  wire comparator_1_gt;

  Comparator #(.width(4), .mode("unsigned")) comparator_1 (.a(A), .b(B), .gt(comparator_1_gt));  // open: eq, lt
  _4bit_swap u_4bit_swap_1 (.I1_4bit(A), .I2_4bit(B), .S(comparator_1_gt), .O1_4bit(out_3), .O2_4bit(out_4));
  // Probe on comparator_1_gt

  // Notes on the sheet:
  //   4bit_2num_sort: import 4bit_swap, comparator
endmodule
