// Logisim project Adder.circ as structural Verilog: 1 circuit, main circuit main
module main (
  input  A,
  input  B,
  input  C_in,
  output S,
  output C_out
);

  wire A_B_2_out, A_B__C_in_out, A_B_out;

  xor A_B (A_B_out, A, B);
  xor A_B_C_in (S, A_B_out, C_in);
  and A_B__C_in (A_B__C_in_out, A_B_out, C_in);
  and A_B_2 (A_B_2_out, A, B);
  or or_1 (C_out, A_B__C_in_out, A_B_2_out);
endmodule
