// Logisim project Fibonacci.circ as structural Verilog: 5 circuits, main circuit main
module main (
  input  [2:0] N,
  output [3:0] Nth
);

  wire clock_1_out, clock_2_out, clock_3_out, comparator_1_eq, Reached_continue;
  wire [2:0] Calc_no_new, init_001_1_out_2, register_1_q;
  wire [3:0] Calc_new, Calc_pre_new, last_q, pre_last_q, Result;

  Iterator Reached (.In(N), .No(init_001_1_out_2), .Continue(Reached_continue));
  Transition Calc (
    .pre_last(pre_last_q), .last(Result), .Continue(Reached_continue), .No_pre(init_001_1_out_2),
    .pre_new(Calc_pre_new), .\new (Calc_new), .No_new(Calc_no_new));
  Comparator #(.width(3)) comparator_1 (.a(N), .b(3'b000), .eq(comparator_1_eq));  // open: gt, lt
  Init_001 init_001_1 (.in_1(register_1_q), .out_2(init_001_1_out_2));
  Register #(.width(3)) register_1 (.D(Calc_no_new), .en(1'b1), .Q(register_1_q), .clk(clock_1_out), .clr(1'b0));
  Clock clock_1 (.out(clock_1_out));
  // Probe on pre_last_q
  Register #(.width(4)) pre_last (.D(Calc_pre_new), .en(1'b1), .Q(pre_last_q), .clk(clock_2_out), .clr(1'b0));
  Clock clock_2 (.out(clock_2_out));
  Register #(.width(4)) last (.D(Calc_new), .en(1'b1), .Q(last_q), .clk(clock_3_out), .clr(1'b0));
  Clock clock_3 (.out(clock_3_out));
  // Probe on init_001_1_out_2
  Multiplexer #(.width(4)) multiplexer_1 (.in0(Result), .in1(4'b0000), .out(Nth), .sel(comparator_1_eq), .en(1'b1));
  // Probe on Result
  Init_0001 init_0001_1 (.in_1(last_q), .out_2(Result));

  // Notes on the sheet:
  //   Fibonacci Calculator: special case on '0'th
endmodule

module Init_0001 (
  input  [3:0] in_1,
  output [3:0] out_2
);

  wire nor_1_out;

  Multiplexer #(.width(4)) multiplexer_1 (.in0(in_1), .in1(4'b0001), .out(out_2), .sel(nor_1_out), .en(1'b1));
  nor nor_1 (nor_1_out, in_1[0], in_1[1], in_1[2], in_1[3]);

  // Notes on the sheet:
  //   4bit Initializer: set R to 0001
endmodule

module Transition (
  input  [3:0] pre_last,
  input  [3:0] last,
  input  Continue,
  input  [2:0] No_pre,
  output [3:0] pre_new,
  output [3:0] \new ,
  output [2:0] No_new
);

  wire [2:0] adder_2_out;
  wire [3:0] adder_1_out;

  Adder #(.width(4)) adder_1 (.a(pre_last), .b(last), .out(adder_1_out));  // open: cin, cout
  // Probe on {pre_last, last}
  Multiplexer #(.width(8)) multiplexer_1 (
    .in0({pre_last, last}), .in1({last, adder_1_out}), .out({pre_new, \new }), .sel(Continue), .en(1'b1));
  // Probe on {last, adder_1_out}
  Adder #(.width(3)) adder_2 (.a(No_pre), .b(3'b001), .out(adder_2_out));  // open: cin, cout
  Multiplexer #(.width(3)) multiplexer_2 (.in0(No_pre), .in1(adder_2_out), .out(No_new), .sel(Continue), .en(1'b1));

  // Notes on the sheet:
  //   Calculator: input continue or not
endmodule

module Iterator (
  input  [2:0] In,
  input  [2:0] No,
  output Continue
);

  Comparator #(.width(3), .mode("unsigned")) comparator_1 (.a(In), .b(No), .gt(Continue));  // open: eq, lt
endmodule

module Init_001 (
  input  [2:0] in_1,
  output [2:0] out_2
);

  wire nor_1_out;

  Multiplexer #(.width(3)) multiplexer_1 (.in0(in_1), .in1(3'b001), .out(out_2), .sel(nor_1_out), .en(1'b1));
  nor nor_1 (nor_1_out, in_1[0], in_1[1], in_1[2]);

  // Notes on the sheet:
  //   3bit Initializer: set No. to 001
endmodule
