// Logisim project Fibonacci_with_MatPow.circ as structural Verilog: 4 circuits, main circuit main
module main (
  input  [31:0] N,
  output [31:0] Nth
);

  wire bitselector_1_out, clock_1_out, clock_2_out, clock_3_out, clock_4_out, clock_5_out, clock_6_out,
       clock_7_out, clock_8_out, clock_9_out, comparator_1_eq, comparator_2_eq, Finished, Keep0_or_Multi1;
  wire [4:0] i;
  wire [5:0] adder_1_out, multiplexer_1_out;
  wire [31:0] _00, _00_prime, _01, _01_prime, _10, _10_prime, _11, _11_prime, A__2_i__00_q, A__2_i__01_q,
       A__2_i__10_q, calc_multi_1_c00, calc_multi_1_c01, calc_multi_1_c10, calc_multi_1_c11,
       calc_square_1_c00, calc_square_1_c01, calc_square_1_c10, calc_square_1_c11, R00, R00_prime, R01,
       R01_prime, R10, R10_prime, R11, R11_prime, Res00_q, Res11_q;

  Adder #(.width(6)) adder_1 (.a({Finished, i}), .b(6'b000001), .out(adder_1_out));  // open: cin, cout
  Comparator #(.width(6), .mode("unsigned")) comparator_1 (
    .a({Finished, i}), .b({6{1'b1}}), .eq(comparator_1_eq));  // open: gt, lt
  Register #(.width(32)) Res00 (.D(R00_prime), .en(1'b1), .Q(Res00_q), .clk(clock_1_out), .clr(1'b0));
  Clock clock_1 (.out(clock_1_out));
  Register #(.width(32)) Res01 (.D(R01_prime), .en(1'b1), .Q(R01), .clk(clock_2_out), .clr(1'b0));
  Clock clock_2 (.out(clock_2_out));
  Register #(.width(32)) Res10 (.D(R10_prime), .en(1'b1), .Q(R10), .clk(clock_3_out), .clr(1'b0));
  Clock clock_3 (.out(clock_3_out));
  Register #(.width(32)) Res11 (.D(R11_prime), .en(1'b1), .Q(Res11_q), .clk(clock_4_out), .clr(1'b0));
  Clock clock_4 (.out(clock_4_out));
  Multiplexer #(.width(6)) multiplexer_1 (
    .in0(adder_1_out), .in1({6{1'b1}}), .out(multiplexer_1_out), .sel(comparator_1_eq), .en(1'b1));
  Clock clock_5 (.out(clock_5_out));
  // Probe on R00
  NumInit_1 numinit_1_1 (.in_1(Res00_q), .out_2(R00));
  // Probe on R01
  // Probe on R10
  // Probe on R11
  NumInit_1 numinit_1_2 (.in_1(Res11_q), .out_2(R11));
  // Probe on {Finished, i}
  Register #(.width(6)) u_i (.D(multiplexer_1_out), .en(1'b1), .Q({Finished, i}), .clk(clock_5_out), .clr(1'b0));
  // Probe on Nth
  Multiplexer #(.width(32)) multiplexer_2 (.in0({32{1'b0}}), .in1(R01), .out(Nth), .sel(Finished), .en(1'b1));
  // Probe on N
  // Probe on {Finished, i}
  Calc_Multi calc_multi_1 (
    .A00(R00), .A01(R01), .A10(R10), .A11(R11), .B00(_00), .B01(_01), .B10(_10), .B11(_11),
    .C00(calc_multi_1_c00), .C01(calc_multi_1_c01), .C10(calc_multi_1_c10), .C11(calc_multi_1_c11));
  BitSelector #(.width(32)) bitselector_1 (.in(N), .out(bitselector_1_out), .sel(i));
  // Probe on i
  // Probe on Keep0_or_Multi1
  Multiplexer multiplexer_3 (.in0(bitselector_1_out), .in1(1'b0), .out(Keep0_or_Multi1), .sel(Finished), .en(1'b1));
  Multiplexer #(.width(32)) multiplexer_4 (
    .in0(R00), .in1(calc_multi_1_c00), .out(R00_prime), .sel(Keep0_or_Multi1), .en(1'b1));
  Multiplexer #(.width(32)) multiplexer_5 (
    .in0(R01), .in1(calc_multi_1_c01), .out(R01_prime), .sel(Keep0_or_Multi1), .en(1'b1));
  Multiplexer #(.width(32)) multiplexer_6 (
    .in0(R10), .in1(calc_multi_1_c10), .out(R10_prime), .sel(Keep0_or_Multi1), .en(1'b1));
  Multiplexer #(.width(32)) multiplexer_7 (
    .in0(R11), .in1(calc_multi_1_c11), .out(R11_prime), .sel(Keep0_or_Multi1), .en(1'b1));
  Clock clock_6 (.out(clock_6_out));
  Clock clock_7 (.out(clock_7_out));
  Clock clock_8 (.out(clock_8_out));
  Clock clock_9 (.out(clock_9_out));
  // Probe on _00
  NumInit_1 numinit_1_3 (.in_1(A__2_i__00_q), .out_2(_00));
  Register #(.width(32)) A__2_i__00 (.D(_00_prime), .en(1'b1), .Q(A__2_i__00_q), .clk(clock_6_out), .clr(1'b0));
  // Probe on _01
  NumInit_1 numinit_1_4 (.in_1(A__2_i__01_q), .out_2(_01));
  Register #(.width(32)) A__2_i__01 (.D(_01_prime), .en(1'b1), .Q(A__2_i__01_q), .clk(clock_7_out), .clr(1'b0));
  // Probe on _10
  Register #(.width(32)) A__2_i__10 (.D(_10_prime), .en(1'b1), .Q(A__2_i__10_q), .clk(clock_8_out), .clr(1'b0));
  NumInit_1 numinit_1_5 (.in_1(A__2_i__10_q), .out_2(_10));
  // Probe on _11
  Register #(.width(32)) A__2_i__11 (.D(_11_prime), .en(1'b1), .Q(_11), .clk(clock_9_out), .clr(1'b0));
  Calc_Square calc_square_1 (
    .A00(_00), .A01(_01), .A10(_10), .A11(_11), .C00(calc_square_1_c00), .C01(calc_square_1_c01),
    .C10(calc_square_1_c10), .C11(calc_square_1_c11));
  Multiplexer #(.width(32)) multiplexer_8 (
    .in0(calc_square_1_c00), .in1(_00), .out(_00_prime), .sel(comparator_2_eq), .en(1'b1));
  Comparator #(.width(5), .mode("unsigned")) comparator_2 (.a(i), .b({5{1'b1}}), .eq(comparator_2_eq));  // open: gt, lt
  Multiplexer #(.width(32)) multiplexer_9 (
    .in0(calc_square_1_c01), .in1(_01), .out(_01_prime), .sel(comparator_2_eq), .en(1'b1));
  Multiplexer #(.width(32)) multiplexer_10 (
    .in0(calc_square_1_c10), .in1(_10), .out(_10_prime), .sel(comparator_2_eq), .en(1'b1));
  Multiplexer #(.width(32)) multiplexer_11 (
    .in0(calc_square_1_c11), .in1(_11), .out(_11_prime), .sel(comparator_2_eq), .en(1'b1));

  // Other names for the same wires on the sheet: i6[5:0] = {Finished, i}

  // Notes on the sheet:
  //   Counter:0,1,2,...,31,...,63
  //   Store the Result A^N Matrix
  //   Initialize: Set to [[1,0],[0,1]] (Identity Matrix)
  //   Travelling all the bits of N
  //   Multi the A^(2^i)s together while travelling the bits of N
  //   Store the A^(2^i) and Update
  //   Initialize: Set to [[1,1],[1,0]] (Fibonacci Matrix)
  //   Calc A^(2^i) = A^(2^(i-1)) ** 2
endmodule

module Calc_Square (
  input  [31:0] A00,
  input  [31:0] A01,
  input  [31:0] A10,
  input  [31:0] A11,
  output [31:0] C00,
  output [31:0] C01,
  output [31:0] C10,
  output [31:0] C11
);

  Calc_Multi Calc_Multi (
    .A00(A00), .A01(A01), .A10(A10), .A11(A11), .B00(A00), .B01(A01), .B10(A10), .B11(A11), .C00(C00),
    .C01(C01), .C10(C10), .C11(C11));
  // Probe on C00
  // Probe on C01
  // Probe on C10
  // Probe on C11

  // Other names for the same wires on the sheet: a[31:0] = A00; b[31:0] = A01; c[31:0] = A10; d[31:0] = A11

  // Notes on the sheet:
  //   Input: 1 Matrix A.   Ouput: 1 Matrix A^2
endmodule

module Calc_Multi (
  input  [31:0] A00,
  input  [31:0] A01,
  input  [31:0] A10,
  input  [31:0] A11,
  input  [31:0] B00,
  input  [31:0] B01,
  input  [31:0] B10,
  input  [31:0] B11,
  output [31:0] C00,
  output [31:0] C01,
  output [31:0] C10,
  output [31:0] C11
);

  wire [31:0] multiplier_1_out, multiplier_2_out, multiplier_3_out, multiplier_4_out, multiplier_5_out,
       multiplier_6_out, multiplier_7_out, multiplier_8_out;

  Multiplier #(.width(32)) multiplier_1 (.a(A00), .b(B00), .out(multiplier_1_out));  // open: cin, cout
  Multiplier #(.width(32)) multiplier_2 (.a(A01), .b(B10), .out(multiplier_2_out));  // open: cin, cout
  Multiplier #(.width(32)) multiplier_3 (.a(A00), .b(B01), .out(multiplier_3_out));  // open: cin, cout
  Multiplier #(.width(32)) multiplier_4 (.a(A01), .b(B11), .out(multiplier_4_out));  // open: cin, cout
  Multiplier #(.width(32)) multiplier_5 (.a(A10), .b(B00), .out(multiplier_5_out));  // open: cin, cout
  Multiplier #(.width(32)) multiplier_6 (.a(A11), .b(B10), .out(multiplier_6_out));  // open: cin, cout
  Multiplier #(.width(32)) multiplier_7 (.a(A10), .b(B01), .out(multiplier_7_out));  // open: cin, cout
  Multiplier #(.width(32)) multiplier_8 (.a(A11), .b(B11), .out(multiplier_8_out));  // open: cin, cout
  // Probe on C00
  Adder #(.width(32)) adder_1 (.a(multiplier_1_out), .b(multiplier_2_out), .out(C00));  // open: cin, cout
  // Probe on C01
  Adder #(.width(32)) adder_2 (.a(multiplier_3_out), .b(multiplier_4_out), .out(C01));  // open: cin, cout
  // Probe on C10
  Adder #(.width(32)) adder_3 (.a(multiplier_5_out), .b(multiplier_6_out), .out(C10));  // open: cin, cout
  // Probe on C11
  Adder #(.width(32)) adder_4 (.a(multiplier_7_out), .b(multiplier_8_out), .out(C11));  // open: cin, cout

  // Other names for the same wires on the sheet: a[31:0] = A00; b[31:0] = A01; c[31:0] = A10; d[31:0] = A11;
  //   w[31:0] = B11; x[31:0] = B00; y[31:0] = B01; z[31:0] = B10

  // Notes on the sheet:
  //   Input: 2 Matrix A,B.   Ouput: 1 Matrix A*B
endmodule

module NumInit_1 (
  input  [31:0] in_1,
  output [31:0] out_2
);

  wire nor_1_out;

  Multiplexer #(.width(32)) multiplexer_1 (.in0(in_1), .in1(32'h1), .out(out_2), .sel(nor_1_out), .en(1'b1));
  nor nor_1 (nor_1_out, in_1[0], in_1[1], in_1[2], in_1[3], in_1[4], in_1[5], in_1[6], in_1[7], in_1[8], in_1[9], in_1[10], in_1[11], in_1[12], in_1[13], in_1[14], in_1[15], in_1[16], in_1[17], in_1[18], in_1[19], in_1[20], in_1[21], in_1[22], in_1[23], in_1[24], in_1[25], in_1[26], in_1[27], in_1[28], in_1[29], in_1[30], in_1[31]);

  // Other names for the same wires on the sheet: _13 = in_1[14]
endmodule
